# Fritzing sketch Fritzing Sketch Source File (saved by Fritzing 0.9.3b)
breadboards: 1

parts:
  Part1 = Arduino Uno (Rev3) - ICSP
  Part2 = HC-SR501 Body Sensor Module
  LED1 = smd LED [color="Red (633nm)" package="1206 [SMD]"]
  R1 = Resistor [tolerance=±5% resistance=220 package="2512 [SMD]"]
  J1 = Piezo Speaker
  J2 = Basic Servo

nets:
  N1: Part1.D8, J1.pin1
  GND: Part1.GND, Part2.GND, R1.Pin_0, J1.pin2, J2.gnd
  N2: Part1.D3_PWM, Part2.OUT
  N3: Part1.D4, LED1.cathode, R1.Pin_1
  N4: Part1.D5_PWM, J2.pulse
  VCC: Part1.5V, Part2.VCC, J2.vcc

notes:
  Developed By Web Dev Fusion
  https://www.webdevfusion.com
  Developed By Web Dev Fusion
  www.webdevfusion.com
  GND - Green
  5VC - Red
  GPIO - Blue

custom parts:
  HC-SR501 Body Sensor Module: Pyroelectric Infrared PIR Motion Sensor Detector Module
